# Fritzing sketch project2 (saved by Fritzing 0.9.4)
breadboards: 1

parts:
  Onderdeel1 = Arduino Uno (Rev3) - ICSP
  Onderdeel2 = Thumb Joystick
  S1 = Pushbutton [package="[THT]"]
  R1 = Resistor [tolerance=±5% resistance=10k package=THT]
  J1 = Piezo Speaker

nets:
  N1: Onderdeel1.A0, Onderdeel2.VERT
  N2: Onderdeel1.A1, Onderdeel2.HORZ
  N3: Onderdeel1.D8, Onderdeel2.SEL
  GND: Onderdeel1.GND, Onderdeel2.GND, R1.Pin_1, J1.pin1
  N4: Onderdeel1.D2, S1.Pin_1, S1.Pin_2, R1.Pin_0
  N5: Onderdeel1.D3_PWM, J1.pin2
  5V: Onderdeel1.5V, Onderdeel2.VCC, S1.Pin_3, S1.Pin_4
